# Fritzing sketch arduino_trumpet (saved by Fritzing 0.9.3b)
breadboards: 1

parts:
  S1 = Pushbutton [package="[THT]"]
  S2 = Pushbutton [package="[THT]"]
  S3 = Pushbutton [package="[THT]"]
  R1 = Resistor [tolerance=±20% resistance=10k package=THT]
  R2 = Resistor [tolerance=±20% resistance=10k package=THT]
  R3 = Resistor [tolerance=±20% resistance=10k package=THT]
  Part1 = Arduino Uno (Rev3)
  J1 = Piezo Speaker

nets:
  N1: S1.Pin_1, S1.Pin_2, R3.Pin_0, Part1.D9_PWM
  N2: S1.Pin_3, S1.Pin_4, S2.Pin_3, S2.Pin_4, S3.Pin_3, S3.Pin_4, Part1.5V
  N3: S2.Pin_1, S2.Pin_2, R2.Pin_0, Part1.D8
  N4: S3.Pin_1, S3.Pin_2, R1.Pin_0, Part1.D10_PWM/SS
  N5: R1.Pin_1, R2.Pin_1, R3.Pin_1, Part1.GND, J1.pin1
  N6: Part1.D7, J1.pin2
