# Fritzing sketch tmp36_led (saved by Fritzing 0.9.3b)
breadboards: 1

parts:
  Part1 = Arduino Uno (Rev3) - ICSP
  T1 = TMP36 Temperature Sensor [package="TO92 [THT]"]
  LED1 = LED - 3mm [color="Red (633nm)" package="3 mm [THT]"]
  R1 = Resistor [tolerance=±5% resistance=220 package=THT]

nets:
  N1: Part1.A0, T1.Vout
  GND: Part1.GND, T1.GND, LED1.cathode
  N2: Part1.D13/SCK, R1.Pin_0
  N3: Part1.5V, T1.+Vs
  N4: LED1.anode, R1.Pin_1
