# Fritzing sketch force_sensor (saved by Fritzing 0.9.3b)
breadboards: 1

parts:
  Part1 = Arduino Uno (Rev3) - ICSP
  J1 = Basic Force Sensing Resistor (FSR) [package=THT]
  R1 = Resistor [tolerance=±5% resistance=220 package=THT]
  R2 = Resistor [tolerance=±5% resistance=220 package="1206 [SMD]"]
  R3 = Resistor [tolerance=±5% resistance=220 package="1206 [SMD]"]
  R4 = Resistor [tolerance=±5% resistance=220 package="1206 [SMD]"]
  R5 = Resistor [tolerance=±5% resistance=220 package="1206 [SMD]"]
  R6 = Resistor [tolerance=±5% resistance=220 package="1206 [SMD]"]
  LED1 = LED - 5mm [color="Red (633nm)" package="5 mm [THT]"]
  LED2 = LED - 5mm [color="Red (633nm)" package="5 mm [THT]"]
  LED3 = smd LED [color="Red (633nm)" package="0603 [SMD]"]
  LED4 = smd LED [color="Red (633nm)" package="0603 [SMD]"]
  LED5 = smd LED [color="Red (633nm)" package="0805 [SMD]"]

nets:
  N1: Part1.A0, J1.pin_0, R1.Pin_1
  N2: Part1.5V, J1.pin_1
  N3: Part1.GND, R1.Pin_0, R2.Pin_1, R3.Pin_1, R4.Pin_1, R5.Pin_1, R6.Pin_1
  N4: Part1.D3_PWM, LED1.anode
  N5: Part1.D4, LED2.anode
  N6: Part1.D5_PWM, LED3.anode
  N7: Part1.D6_PWM, LED4.anode
  N8: Part1.D7, LED5.anode
  N9: R2.Pin_0, LED1.cathode
  N10: R3.Pin_0, LED2.cathode
  N11: R4.Pin_0, LED5.cathode
  N12: R5.Pin_0, LED4.cathode
  N13: R6.Pin_0, LED3.cathode
