# Fritzing sketch lab9 (saved by Fritzing 0.9.3b)
breadboards: 1

parts:
  Part1 = Arduino Uno (Rev3)
  J1 = Piezo Speaker
  hc-sr1 = hc-sr04

nets:
  N1: Part1.D10_PWM/SS, hc-sr1.Echo
  N2: Part1.D11_PWM/MOSI, hc-sr1.Trig
  N3: Part1.D5_PWM, J1.pin1
  5V: Part1.5V, hc-sr1.VCC
  GND: Part1.GND, J1.pin2, hc-sr1.GND

notes:
  + Side
  - Side
